# Fritzing sketch project (saved by Fritzing 0.9.2b)

parts:
  Part1 = FC-28 Soil Hygrometer Module - Probe
  Part2 = FC-28 Soil Hygrometer Module
  U1 = NodeMCU V1.0

nets:
  N1: Part1.POS, Part2.POS
  N2: Part1.NEG, Part2.NEG
  VCC: Part2.VCC, U1.3V3
  GND: Part2.GND, U1.GND
  N3: Part2.AO, U1.D4
  N4: U1.D0, U1.RST

custom parts:
  FC-28 Soil Hygrometer Module - Probe: The FC-28 is a soil hygrometer module that uses the Texas Instruments LM393 comparator chip to provide an analog measurement of soil humidity.
  FC-28 Soil Hygrometer Module: The FC-28 is a soil hygrometer module that uses the Texas Instruments LM393 comparator chip to provide an analog measurement of soil humidity. The digital output is high when soil moisture is over a certain threshold, as determined by adjusting the potentiometer.
  NodeMCU V1.0: ESP8266 based NodeMCU
